// Logisim project circuito.circ as structural Verilog: 3 circuits, main circuit main
module main (
);

  wire [7:0] PC_q;

  Register PC (.Q(PC_q));  // open: D, en, clk, clr
  ROM rom_1 (.addr(PC_q));  // open: data
  banco_de_registradores banco_de_registradores_1 ();  // open: Dado, WE, RD, RB, RS1, RS2
  ULA ula_1 ();  // open: A, B, Funct, S
  RAM ram_1 ();  // open: addr, we, oe, clk, din, dout
endmodule

module banco_de_registradores (
  input  [11:0] Dado,
  input  WE,
  input  [3:0] RD,
  input  [3:0] RB,
  output [11:0] RS1,
  output [11:0] RS2
);

  wire Er1, Er2, Er3, Er4, Er5, Er6, Er7, Er8, Er9, Er10, Er11, Er12, Er13, Er14, Er15, Er16;
  wire [11:0] register_1_q, register_2_q, register_3_q, register_4_q, register_5_q, register_6_q,
       register_7_q, register_8_q, register_9_q, register_10_q, register_11_q, register_12_q, register_13_q,
       register_14_q, register_15_q, register_16_q;

  Demultiplexer #(.select(4)) demultiplexer_1 (
    .out0(Er1), .out1(Er2), .out2(Er3), .out3(Er4), .out4(Er5), .out5(Er6), .out6(Er7), .out7(Er8),
    .out8(Er9), .out9(Er10), .out10(Er11), .out11(Er12), .out12(Er13), .out13(Er14), .out14(Er15),
    .out15(Er16), .in(WE), .sel(RD));
  Register #(.width(12)) register_1 (.D(Dado), .en(Er1), .Q(register_1_q));  // open: clk, clr
  Register #(.width(12)) register_2 (.D(Dado), .en(Er2), .Q(register_2_q));  // open: clk, clr
  Register #(.width(12)) register_3 (.D(Dado), .en(Er3), .Q(register_3_q));  // open: clk, clr
  Register #(.width(12)) register_4 (.D(Dado), .en(Er4), .Q(register_4_q));  // open: clk, clr
  Register #(.width(12)) register_5 (.D(Dado), .en(Er5), .Q(register_5_q));  // open: clk, clr
  Register #(.width(12)) register_6 (.D(Dado), .en(Er6), .Q(register_6_q));  // open: clk, clr
  Register #(.width(12)) register_7 (.D(Dado), .en(Er7), .Q(register_7_q));  // open: clk, clr
  Register #(.width(12)) register_8 (.D(Dado), .en(Er8), .Q(register_8_q));  // open: clk, clr
  Multiplexer #(.select(4), .width(12)) multiplexer_1 (
    .in0(register_1_q), .in1(register_2_q), .in2(register_3_q), .in3(register_4_q), .in4(register_5_q),
    .in5(register_6_q), .in6(register_7_q), .in7(register_8_q), .in8(register_9_q), .in9(register_10_q),
    .in10(register_11_q), .in11(register_12_q), .in12(register_13_q), .in13(register_14_q),
    .in14(register_15_q), .in15(register_16_q), .out(RS1), .sel(RD));
  Register #(.width(12)) register_9 (.D(Dado), .en(Er9), .Q(register_9_q));  // open: clk, clr
  Register #(.width(12)) register_10 (.D(Dado), .en(Er10), .Q(register_10_q));  // open: clk, clr
  Register #(.width(12)) register_11 (.D(Dado), .en(Er11), .Q(register_11_q));  // open: clk, clr
  Register #(.width(12)) register_12 (.D(Dado), .en(Er12), .Q(register_12_q));  // open: clk, clr
  Multiplexer #(.select(4), .width(12)) multiplexer_2 (
    .in0(register_1_q), .in1(register_2_q), .in2(register_3_q), .in3(register_4_q), .in4(register_5_q),
    .in5(register_6_q), .in6(register_7_q), .in7(register_8_q), .in8(register_9_q), .in9(register_10_q),
    .in10(register_11_q), .in11(register_12_q), .in12(register_13_q), .in13(register_14_q),
    .in14(register_15_q), .in15(register_16_q), .out(RS2), .sel(RB));
  Register #(.width(12)) register_13 (.D(Dado), .en(Er13), .Q(register_13_q));  // open: clk, clr
  Register #(.width(12)) register_14 (.D(Dado), .en(Er14), .Q(register_14_q));  // open: clk, clr
  Register #(.width(12)) register_15 (.D(Dado), .en(Er15), .Q(register_15_q));  // open: clk, clr
  Register #(.width(12)) register_16 (.D(Dado), .en(Er16), .Q(register_16_q));  // open: clk, clr
endmodule

module ULA (
  input  [11:0] A,
  input  [11:0] B,
  input  [1:0] Funct,
  output [11:0] S
);

  wire [11:0] adder_1_out, and_1_out, or_1_out, subtractor_1_out, undriven;

  Adder #(.width(12)) adder_1 (.a(A), .b(B), .out(adder_1_out));  // open: cin, cout
  Subtractor #(.width(12)) subtractor_1 (.a(A), .b(B), .out(subtractor_1_out));  // open: bin, bout
  assign and_1_out = A & B;  // AND_Gate and_1, 12 bits wide
  assign or_1_out = A | B;  // OR_Gate or_1, 12 bits wide
  Multiplexer #(.select(2), .width(12)) multiplexer_1 (.in0(undriven), .out(S), .sel(Funct));  // open: in1, in2, in3
endmodule
